# Fritzing sketch Nik Circuit (saved by Fritzing 0.9.3b)
breadboards: 1

parts:
  WATER_PUMP1 = water pump/motor  # not connected
  Part1 = Jtron 1 Channel Optoisolated Relay Module [package=relay]
  M1 = ph-4502c [package=THT]
  Part2 = Arduino Uno (Rev3)

nets:
  VCC: Part1.VCC, Part1.MAIN, M1.pin6, Part2.5V
  N1: Part1.IN1, Part2.D3_PWM
  GND: Part1.GND, M1.pin4, M1.pin5, Part2.GND
  N2: M1.pin3, Part2.A0

custom parts:
  water pump/motor: WATER PUMP BY ARDUBLOCKTR
  ph-4502c: ph-4502c PH Meter.
